// Logisim project 8085_Microprocessor.circ as structural Verilog: 17 circuits, main circuit main
module main (
  input  in_1,
  input  in_2
);

  wire ac_15_t, AC_load, and_28_out, and_29_out, AR_load, B0, B1, B2, B3, B4, B5, B6, B7, B8, B9, B10, B11,
       Clk, common_bus_1_e_out, D0, D0T4, D0T5, D1, D1T4, D1T5, D2, D2T4, D2T5, D3, D3T4, D4, D4T4, D5, D5T4,
       D5T5, D6, D6T4, D6T5, D6T6, D7, De0, De1, De2, DR_load, E, I, I_ff, Ind, ISZ, multiplexer_1_out,
       not_1_out, not_2_out, not_3_out, not_4_out, not_5_out, not_6_out, or_14_out, or_15_out, PC_inr,
       PC_load, r, R0, R1, R2, R3, R4, R5, R6, R7, R8, R9, R10, R11, rst, SC_inr, SZA, T0, T1, T2, T3, T4,
       T5, T6, w, x1, x2, x3, x4, x5;
  wire [1:0] E_sel;
  wire [2:0] ALU, Source;
  wire [11:0] common_bus_1_ar;
  wire [15:0] AC, common_bus_1_pc, DR;

  Clock clock_1 (.out(Clk));
  and and_1 (R0, r, B0);
  and and_2 (R1, r, B1);
  and and_3 (R2, r, B2);
  and and_4 (R3, r, B3);
  and and_5 (R4, r, B4);
  and and_6 (R5, r, B5);
  or or_1 (x1, D0T4, D1T4, D2T4, D6T4, T1, r, Ind);
  or or_2 (x2, D5T5, D4T4);
  or or_3 (x3, D5T4, T0);
  or or_4 (x4, D0T5, D1T5, D2T5, D6T6);
  Decoder #(.enable("false"), .select(3)) decoder_1 (
    .out0(D0), .out1(D1), .out2(D2), .out3(D3), .out4(D4), .out5(D5), .out6(D6), .out7(D7),
    .sel({De2, De1, De0}));
  and and_7 (R6, r, B6);
  and and_8 (R7, r, B7);
  and and_9 (R8, r, B8);
  and and_10 (R9, r, B9);
  and and_11 (R10, r, B10);
  and and_12 (R11, r, B11);
  not not_1 (not_1_out, I);
  or or_5 (rst, D0T5, D1T5, D2T5, D3T4, D4T4, D5T5, D6T6, R0, r);
  or or_6 (w, D3T4, D5T4, D6T6);
  SeqCounter seqcounter_1 (
    .INR(SC_inr), .CLR(rst), .CLK(Clk), .T0(T0), .T1(T1), .T2(T2), .T3(T3), .T4(T4), .T5(T5), .T6(T6));
  Multiplexer multiplexer_1 (.in0(I), .in1(I_ff), .out(multiplexer_1_out), .sel(T2));
  and and_13 (r, not_1_out, D7, T3);
  and and_14 (D0T4, D0, T4);
  and and_15 (D0T5, D0, T5);
  and and_16 (D1T4, D1, T4);
  and and_17 (D1T5, D1, T5);
  and and_18 (D2T4, D2, T4);
  and and_19 (D2T5, D2, T5);
  not not_2 (not_2_out, D7);
  D_Flip_Flop d_ff_1 (.D(multiplexer_1_out), .clk(Clk), .Q(I));  // open: Qn, preset, reset
  and and_20 (Ind, not_2_out, I, T3);
  or or_7 (PC_load, D5T5, D4T4);
  or or_8 (DR_load, D0T4, D1T4, D2T4, D6T4);
  and and_21 (D3T4, D3, T4);
  and and_22 (D4T4, D4, T4);
  and and_23 (D5T4, D5, T4);
  and and_24 (D5T5, D5, T5);
  and and_25 (D6T4, D6, T4);
  and and_26 (D6T5, D6, T5);
  and and_27 (D6T6, D6, T6);
  or or_9 (AR_load, T0, T2, Ind);
  // Probe on {I_ff, De2, De1, De0, B11, B10, B9, B8, B7, B6, B5, B4, B3, B2, B1, B0}
  and and_28 (and_28_out, R3, AC[15]);
  not not_3 (not_3_out, AC[15]);
  and and_29 (and_29_out, not_3_out, R4);
  or or_10 (ac_15_t, and_28_out, and_29_out);
  or or_11 (x5, D3T4, D1T5, D0T5);
  StartSwitch startswitch_1 (.Start(in_1), .rst(rst), .Clk(Clk), .SC_inr(SC_inr));
  Bus_Select bus_select_1 (.x1(x1), .x2(x2), .x3(x3), .x4(x4), .x5(x5), .x6(T2), .Source(Source));
  Alu_Select alu_select_1 (.A1(D0T5), .A2(D1T5), .A3(D2T5), .A4(R9), .A5(R7), .A6(R6), .Alu_Select(ALU));
  E_Select e_select_1 (.E1(D1T5), .E2(R7), .E3(R6), .AB(E_sel));
  // Probe on Source
  // Probe on ALU
  // Probe on E_sel
  or or_12 (PC_inr, T1, R1, R2, R3, R4, E, ISZ, SZA, ac_15_t);
  or or_13 (AC_load, D1T5, D0T5, D2T5, R6, R7, R9);
  Common_Bus common_bus_1 (
    .Write(w), .Read(x1), .clk(Clk), .ALU_select(ALU), .AR_inr(D5T4), .AR_load(AR_load), .Source(Source),
    .PC_inr(PC_inr), .PC_clr(in_2), .PC_load(PC_load), .DR_inr(D6T5), .DR_load(DR_load), .AC_inr(R5),
    .AC_clr(R11), .AC_load(AC_load), .IR_load(T1), .E_clr(R10), .E_comp(R8), .E_load(D1T5), .E_select(E_sel),
    .AR(common_bus_1_ar), .PC(common_bus_1_pc), .DR(DR), .AC_out(AC),
    .IR({I_ff, De2, De1, De0, B11, B10, B9, B8, B7, B6, B5, B4, B3, B2, B1, B0}), .E_out(common_bus_1_e_out));  // open: AR_clr, DR_clr, TR_inr, TR_clr, TR_load
  // Probe on common_bus_1_ar
  // Probe on common_bus_1_pc
  not not_4 (not_4_out, common_bus_1_e_out);
  and and_30 (E, not_4_out, R1);
  // Probe on common_bus_1_e_out
  // Probe on DR
  // Probe on {I_ff, De2, De1, De0, B11, B10, B9, B8, B7, B6, B5, B4, B3, B2, B1, B0}
  or or_14 (or_14_out, AC[15], AC[14], AC[13], AC[12], AC[11], AC[10], AC[9], AC[8], AC[7], AC[6], AC[5], AC[4], AC[3], AC[2], AC[1], AC[0]);
  or or_15 (or_15_out, DR[15], DR[14], DR[13], DR[12], DR[11], DR[10], DR[9], DR[8], DR[7], DR[6], DR[5], DR[4], DR[3], DR[2], DR[1], DR[0]);
  // Probe on AC
  not not_5 (not_5_out, or_14_out);
  not not_6 (not_6_out, or_15_out);
  and and_31 (SZA, not_5_out, R2);
  and and_32 (ISZ, not_6_out, D6T6);

  // Other names for the same wires on the sheet: AC_15 = AC[15]; clr = in_2;
  //   IR[15:0] = {I_ff, De2, De1, De0, B11, B10, B9, B8, B7, B6, B5, B4, B3, B2, B1, B0}; Strt = in_1

  // Notes on the sheet:
  //   Instructions decoding
  //   Bus select
endmodule

module StartSwitch (
  input  Start,
  input  rst,
  input  Clk,
  output SC_inr
);

  wire and_1_out, not_1_out, or_1_out;

  not not_1 (not_1_out, rst);
  and and_1 (and_1_out, not_1_out, SC_inr);
  or or_1 (or_1_out, Start, and_1_out);
  D_Flip_Flop d_ff_1 (.D(or_1_out), .clk(Clk), .Q(SC_inr));  // open: Qn, preset, reset
endmodule

module Common_Bus (
  input  Write,
  input  Read,
  input  clk,
  input  [2:0] ALU_select,
  input  AR_inr,
  input  AR_clr,
  input  AR_load,
  input  [2:0] Source,
  input  PC_inr,
  input  PC_clr,
  input  PC_load,
  input  DR_inr,
  input  DR_clr,
  input  DR_load,
  input  AC_inr,
  input  AC_clr,
  input  AC_load,
  input  IR_load,
  input  TR_inr,
  input  TR_clr,
  input  TR_load,
  input  E_clr,
  input  E_comp,
  input  E_load,
  input  [1:0] E_select,
  output [11:0] AR,
  output [15:0] PC,
  output [15:0] DR,
  output [15:0] AC_out,
  output [15:0] IR,
  output E_out
);

  wire Cout, multiplexer_1_out;
  wire [11:0] bit_16to12_1_out_12;
  wire [15:0] ALU_out, bit_12to16_1_out_16, multiplexer_2_out, ram_1_dout, temporaryregister_1_dataout;

  Multiplexer #(.select(2)) multiplexer_1 (
    .in1(Cout), .in2(AC_out[0]), .in3(AC_out[15]), .out(multiplexer_1_out), .sel(E_select));  // open: in0
  // Probe on AR
  Bit_16to12 bit_16to12_1 (.in_16(multiplexer_2_out), .out_12(bit_16to12_1_out_12));
  RAM #(.addrWidth(12), .asyncread("true"), .dataWidth(16)) ram_1 (
    .addr(AR), .we(Write), .oe(Read), .clk(clk), .din(multiplexer_2_out), .dout(ram_1_dout));
  AddressRegister addressregister_1 (
    .INR(AR_inr), .CLR(AR_clr), .LOAD(AR_load), .CLK(clk), .DataIn(bit_16to12_1_out_12), .DataOut(AR));
  ProgramCounter programcounter_1 (
    .INR(PC_inr), .CLR(PC_clr), .LOAD(PC_load), .CLK(clk), .DataIn(multiplexer_2_out), .DataOut(PC));
  DataRegister dataregister_1 (
    .INR(DR_inr), .CLR(DR_clr), .LOAD(DR_load), .CLK(clk), .DataIn(multiplexer_2_out), .DataOut(DR));
  Accumulator accumulator_1 (.INR(AC_inr), .CLR(AC_clr), .LOAD(AC_load), .CLK(clk), .DataIn(ALU_out), .Dataout(AC_out));
  InstructionRegister instructionregister_1 (.DataIn(multiplexer_2_out), .load(IR_load), .clk(clk), .DataOut(IR));
  TemporaryRegister temporaryregister_1 (
    .INR(TR_inr), .CLR(TR_clr), .LOAD(TR_load), .CLK(clk), .DataIn(multiplexer_2_out),
    .DataOut(temporaryregister_1_dataout));
  ERegister eregister_1 (
    .clr(E_clr), .Com_E(E_comp), .load(E_load), .clk(clk), .DataIn(multiplexer_1_out), .E_ff_op(E_out));
  BIT_12to16 bit_12to16_1 (.in_12(AR), .out_16(bit_12to16_1_out_16));
  // Probe on bit_12to16_1_out_16
  // Probe on multiplexer_2_out
  Multiplexer #(.select(3), .width(16)) multiplexer_2 (
    .in1(ram_1_dout), .in2(bit_12to16_1_out_16), .in3(PC), .in4(DR), .in5(AC_out), .in6(IR),
    .in7(temporaryregister_1_dataout), .out(multiplexer_2_out), .sel(Source));  // open: in0
  // Probe on AC_out
  // Probe on DR
  ALU alu_1 (.AC(AC_out), .DR(DR), .Alu_select(ALU_select), .ER(E_out), .EL(E_out), .ALU_out(ALU_out), .Cout(Cout));

  // Other names for the same wires on the sheet: AC_0 = AC_out[0]; AC_15 = AC_out[15]; AR_out[11:0] = AR;
  //   DR_out[15:0] = DR; E_ff = E_out

  // Notes on the sheet:
  //   COMMON_BUS
endmodule

module SeqCounter (
  input  INR,
  input  CLR,
  input  CLK,
  output T0,
  output T1,
  output T2,
  output T3,
  output T4,
  output T5,
  output T6
);

  wire [2:0] adder_1_out, multiplexer_1_out, multiplexer_2_out, register_1_q;

  Adder #(.width(3)) adder_1 (.a(register_1_q), .b(3'b001), .out(adder_1_out));  // open: cin, cout
  Multiplexer #(.width(3)) multiplexer_1 (.in0(register_1_q), .in1(adder_1_out), .out(multiplexer_1_out), .sel(INR));
  Multiplexer #(.width(3)) multiplexer_2 (.in0(multiplexer_1_out), .in1(3'b000), .out(multiplexer_2_out), .sel(CLR));
  Register #(.width(3)) register_1 (.D(multiplexer_2_out), .clk(CLK), .Q(register_1_q));  // open: en, clr
  Decoder #(.enable("false"), .select(3)) decoder_1 (
    .out1(T0), .out2(T1), .out3(T2), .out4(T3), .out5(T4), .out6(T5), .out7(T6), .sel(register_1_q));  // open: out0
endmodule

module AddressRegister (
  input  INR,
  input  CLR,
  input  LOAD,
  input  CLK,
  input  [11:0] DataIn,
  output [11:0] DataOut
);

  wire [11:0] adder_1_out, multiplexer_1_out, multiplexer_2_out, multiplexer_3_out;

  Adder #(.width(12)) adder_1 (.a(DataOut), .b(12'h1), .out(adder_1_out));  // open: cin, cout
  Multiplexer #(.width(12)) multiplexer_1 (.in0(DataOut), .in1(adder_1_out), .out(multiplexer_1_out), .sel(INR));
  Multiplexer #(.width(12)) multiplexer_2 (
    .in0(multiplexer_1_out), .in1({12{1'b0}}), .out(multiplexer_2_out), .sel(CLR));
  Multiplexer #(.width(12)) multiplexer_3 (.in0(multiplexer_2_out), .in1(DataIn), .out(multiplexer_3_out), .sel(LOAD));
  Register #(.width(12)) register_1 (.D(multiplexer_3_out), .clk(CLK), .Q(DataOut));  // open: en, clr

  // Notes on the sheet:
  //   Address Register
endmodule

module ProgramCounter (
  input  INR,
  input  CLR,
  input  LOAD,
  input  CLK,
  input  [15:0] DataIn,
  output [15:0] DataOut
);

  wire [11:0] adder_1_out, multiplexer_1_out, multiplexer_2_out, multiplexer_3_out;

  Adder #(.width(12)) adder_1 (.a(DataOut[11:0]), .b(12'h1), .out(adder_1_out));  // open: cin, cout
  Multiplexer #(.width(12)) multiplexer_1 (.in0(DataOut[11:0]), .in1(adder_1_out), .out(multiplexer_1_out), .sel(INR));
  Multiplexer #(.width(12)) multiplexer_2 (
    .in0(multiplexer_1_out), .in1({12{1'b0}}), .out(multiplexer_2_out), .sel(CLR));
  Register #(.width(12)) register_1 (.D(multiplexer_3_out), .clk(CLK), .Q(DataOut[11:0]));  // open: en, clr
  Multiplexer #(.width(12)) multiplexer_3 (
    .in0(multiplexer_2_out), .in1(DataIn[11:0]), .out(multiplexer_3_out), .sel(LOAD));

  assign DataOut[15:12] = 4'b0000;

  // Notes on the sheet:
  //   Program Counter
endmodule

module DataRegister (
  input  INR,
  input  CLR,
  input  LOAD,
  input  CLK,
  input  [15:0] DataIn,
  output [15:0] DataOut
);

  wire [15:0] adder_1_out, multiplexer_1_out, multiplexer_2_out, multiplexer_3_out;

  Adder #(.width(16)) adder_1 (.a(DataOut), .b(16'h1), .out(adder_1_out));  // open: cin, cout
  Multiplexer #(.width(16)) multiplexer_1 (.in0(DataOut), .in1(adder_1_out), .out(multiplexer_1_out), .sel(INR));
  Multiplexer #(.width(16)) multiplexer_2 (
    .in0(multiplexer_1_out), .in1({16{1'b0}}), .out(multiplexer_2_out), .sel(CLR));
  Register #(.width(16)) register_1 (.D(multiplexer_3_out), .clk(CLK), .Q(DataOut));  // open: en, clr
  Multiplexer #(.width(16)) multiplexer_3 (.in0(multiplexer_2_out), .in1(DataIn), .out(multiplexer_3_out), .sel(LOAD));

  // Notes on the sheet:
  //   DATA REGISTER
endmodule

module Accumulator (
  input  INR,
  input  CLR,
  input  LOAD,
  input  CLK,
  input  [15:0] DataIn,
  output [15:0] Dataout
);

  wire [15:0] adder_1_out, multiplexer_1_out, multiplexer_2_out, multiplexer_3_out;

  Multiplexer #(.width(16)) multiplexer_1 (.in0(Dataout), .in1(adder_1_out), .out(multiplexer_1_out), .sel(INR));
  Adder #(.width(16)) adder_1 (.a(Dataout), .b(16'h1), .out(adder_1_out));  // open: cin, cout
  Multiplexer #(.width(16)) multiplexer_2 (
    .in0(multiplexer_1_out), .in1({16{1'b0}}), .out(multiplexer_2_out), .sel(CLR));
  Multiplexer #(.width(16)) multiplexer_3 (.in0(multiplexer_2_out), .in1(DataIn), .out(multiplexer_3_out), .sel(LOAD));
  Register #(.width(16)) register_1 (.D(multiplexer_3_out), .clk(CLK), .Q(Dataout));  // open: en, clr

  // Notes on the sheet:
  //   Accumulator
endmodule

module InstructionRegister (
  input  [15:0] DataIn,
  input  load,
  input  clk,
  output [15:0] DataOut
);

  wire [15:0] multiplexer_1_out;

  Multiplexer #(.width(16)) multiplexer_1 (.in0(DataOut), .in1(DataIn), .out(multiplexer_1_out), .sel(load));
  Register #(.width(16)) register_1 (.D(multiplexer_1_out), .clk(clk), .Q(DataOut));  // open: en, clr

  // Notes on the sheet:
  //   Instruction Register
endmodule

module TemporaryRegister (
  input  INR,
  input  CLR,
  input  LOAD,
  input  CLK,
  input  [15:0] DataIn,
  output [15:0] DataOut
);

  wire [15:0] adder_1_out, multiplexer_1_out, multiplexer_2_out, multiplexer_3_out;

  Adder #(.width(16)) adder_1 (.a(DataOut), .b(16'h1), .out(adder_1_out));  // open: cin, cout
  Multiplexer #(.width(16)) multiplexer_1 (.in0(DataOut), .in1(adder_1_out), .out(multiplexer_1_out), .sel(INR));
  Multiplexer #(.width(16)) multiplexer_2 (
    .in0(multiplexer_1_out), .in1({16{1'b0}}), .out(multiplexer_2_out), .sel(CLR));
  Multiplexer #(.width(16)) multiplexer_3 (.in0(multiplexer_2_out), .in1(DataIn), .out(multiplexer_3_out), .sel(LOAD));
  Register #(.width(16)) register_1 (.D(multiplexer_3_out), .clk(CLK), .Q(DataOut));  // open: en, clr

  // Notes on the sheet:
  //   Temporary Register
endmodule

module ERegister (
  input  clr,
  input  Com_E,
  input  load,
  input  clk,
  input  DataIn,
  output E_ff_op
);

  wire multiplexer_1_out, multiplexer_2_out, multiplexer_3_out, not_1_out;

  not not_1 (not_1_out, E_ff_op);
  Multiplexer multiplexer_1 (.in0(E_ff_op), .in1(not_1_out), .out(multiplexer_1_out), .sel(Com_E));
  Multiplexer multiplexer_2 (.in0(multiplexer_1_out), .in1(1'b0), .out(multiplexer_2_out), .sel(clr));
  Multiplexer multiplexer_3 (.in0(multiplexer_2_out), .in1(DataIn), .out(multiplexer_3_out), .sel(load));
  D_Flip_Flop d_ff_1 (.D(multiplexer_3_out), .clk(clk), .Q(E_ff_op));  // open: Qn, preset, reset
endmodule

module ALU (
  input  [15:0] AC,
  input  [15:0] DR,
  input  [2:0] Alu_select,
  input  ER,
  input  EL,
  output [15:0] ALU_out,
  output Cout
);

  wire [15:0] adder_1_out, and_1_out, not_1_out;

  Adder #(.width(16)) adder_1 (.a(DR), .b(AC), .out(adder_1_out), .cout(Cout));  // open: cin
  assign and_1_out = DR & AC;  // AND_Gate and_1, 16 bits wide
  assign not_1_out = ~AC;  // NOT_Gate not_1, 16 bits wide
  Multiplexer #(.select(3), .width(16)) multiplexer_1 (
    .in1(and_1_out), .in2(adder_1_out), .in3(DR), .in4(not_1_out), .in5({ER, AC[15:1]}),
    .in6({AC[14:0], EL}), .out(ALU_out), .sel(Alu_select));  // open: in0, in7

  // Notes on the sheet:
  //   right
  //   left
endmodule

module Bit_16to12 (
  input  [15:0] in_16,
  output [11:0] out_12
);


  assign out_12 = in_16[11:0];
endmodule

module BIT_12to16 (
  input  [11:0] in_12,
  output [15:0] out_16
);


  assign out_16 = {4'b0000, in_12};
endmodule

module Bus_Select (
  input  x1,
  input  x2,
  input  x3,
  input  x4,
  input  x5,
  input  x6,
  output [2:0] Source
);

  or or_1 (Source[0], x1, x3, x5, 1'b0);
  or or_2 (Source[1], x2, x3, x6, 1'b0);
  or or_3 (Source[2], x4, x5, x6, 1'b0);

  // Notes on the sheet:
  //   x3 -> DR
  //   x4 -> AC
  //   x5 -> IR
  //   x6 -> TR
  //   x7 -> Memory
  //   x1 -> AR
  //   x2 -> PC
  //   C
  //   B
  //   A
  //   ABC
endmodule

module Alu_Select (
  input  A1,
  input  A2,
  input  A3,
  input  A4,
  input  A5,
  input  A6,
  output [2:0] Alu_Select
);

  or or_1 (Alu_Select[0], A1, A3, A5);
  or or_2 (Alu_Select[1], A2, A3, A6);
  or or_3 (Alu_Select[2], A4, A5, A6);

  // Notes on the sheet:
  //   x1 -> AND
  //   x2 -> ADD
  //   x4 -> COMP
  //   x5 -> RIGHT SHIFT
  //   x6 -> LEFT SHIFT
  //   x3-> LOAD
  //   C
  //   B
  //   A
  //   ABC
endmodule

module E_Select (
  input  E1,
  input  E2,
  input  E3,
  output [1:0] AB
);

  or or_1 (AB[0], E1, E3);
  or or_2 (AB[1], E2, E3);

  // Other names for the same wires on the sheet: x1 = E1; x2 = E2; x3 = E3

  // Notes on the sheet:
  //   B
  //   A
endmodule
